# Fritzing sketch macchina (saved by Fritzing 0.9.3b)
breadboards: 1

parts:
  Componente1 = Arduino Uno (Rev3)
  IC1 = L293D [package=THT]
  Componente2 = Breadboard Power Supply Board SMD
  VCC1 = Battery block 9V
  hc-sr1 = hc-sr04
  hc-sr2 = hc-sr04
  hc-sr3 = hc-sr04
  hc-sr4 = hc-sr04
  M2 = DC Motor
  M3 = DC Motor
  IR1 = TSOP312.., 314.. [package=THT]
  R1 = Resistor [tolerance=±5% resistance=220 package=THT]
  R2 = Resistor [tolerance=±5% resistance=5.1k package=THT]
  R3 = Resistor [tolerance=±5% resistance=1k package=THT]
  LED1 = LEDs [package=led10mm]
  LED2 = LEDs [package=led10mm]
  LED3 = LEDs [package=led10mm]

nets:
  N1: Componente1.A0, hc-sr4.Trig
  N2: Componente1.A1, hc-sr4.Echo
  N3: Componente1.A2, hc-sr3.Trig
  N4: Componente1.A3, hc-sr3.Echo
  N5: Componente1.A4/SDA, IR1.Data
  N6: Componente1.A5/SCL, R3.Pin_1
  N7: Componente1.D8, hc-sr2.Trig
  N8: Componente1.D9_PWM, IC1.Enable_2
  N9: Componente1.D10_PWM/SS, hc-sr1.Trig
  N10: Componente1.D11_PWM/MOSI, R2.Pin_1
  N11: Componente1.D12/MISO, hc-sr2.Echo
  N12: Componente1.D13/SCK, hc-sr1.Echo
  GND: Componente1.GND, IC1.0V, Componente2.GND, VCC1.-, hc-sr1.GND, hc-sr2.GND, hc-sr3.GND, hc-sr4.GND, IR1.GND, LED1.A, LED2.A, LED3.A
  N13: Componente1.D2, IC1.In_4
  N14: Componente1.D3_PWM, R1.Pin_1
  N15: Componente1.D4, IC1.In_1
  N16: Componente1.D5_PWM, IC1.Enable_1
  N17: Componente1.D6_PWM, IC1.In_2
  N18: Componente1.D7, IC1.In_3
  VCC: Componente1.5V, IC1.+Vmotor, IC1.+V, Componente2.VCC, hc-sr1.VCC, hc-sr2.VCC, hc-sr3.VCC, hc-sr4.VCC, IR1.Vs
  N19: IC1.Out_1_(_Controlled_by_Enable_1_), M3.pin_1
  N20: IC1.Out_2_(_Controlled_by_Enable_1_), M3.pin_2
  N21: IC1.Out_3_(_Controlled_by_Enable_2_), M2.pin_2
  N22: IC1.Out_4_(_Controlled_by_Enable_2_), M2.pin_1
  N23: Componente2.VIN, VCC1.+
  N24: R1.Pin_0, LED1.C
  N25: R2.Pin_0, LED2.C
  N26: R3.Pin_0, LED3.C
